// Logisim project SECONDLAB.circ as structural Verilog: 1 circuit, main circuit main
module main (
  input  [7:0] in_1,
  input  [1:0] in_2
);

  wire decoder_1_out0, decoder_1_out1, decoder_1_out2, decoder_1_out3;

  Decoder #(.select(2)) decoder_1 (
    .out0(decoder_1_out0), .out1(decoder_1_out1), .out2(decoder_1_out2), .out3(decoder_1_out3), .sel(in_2));  // open: en
  RAM ram_1 (.addr(in_1), .sel(decoder_1_out3));  // open: data, clk, ld, clr
  RAM ram_2 (.addr(in_1), .sel(decoder_1_out2));  // open: data, clk, ld, clr
  RAM ram_3 (.addr(in_1), .sel(decoder_1_out1));  // open: data, clk, ld, clr
  RAM ram_4 (.addr(in_1), .sel(decoder_1_out0));  // open: data, clk, ld, clr

  // Notes on the sheet:
  //   MANOJ KUMAR
  //   1803210090
  //   HALF ADDER
endmodule
